// Logisim project IF_ID.circ as structural Verilog: 1 circuit, main circuit main
module main (
  input  [31:0] PC_4,
  input  [31:0] Instruction,
  input  CLK,
  output [31:0] PC_4_2,
  output [31:0] Instruction_2
);

  Register #(.width(32)) register_1 (.D(PC_4), .Q(PC_4_2), .clk(CLK));  // open: en, clr
  Register #(.width(32)) register_2 (.D(Instruction), .Q(Instruction_2), .clk(CLK));  // open: en, clr

  // Other names for the same wires on the sheet: Instruction_Out[31:0] = Instruction_2; PC_4_Out[31:0] = PC_4_2
endmodule
